# Fritzing sketch circuito-architettura1 (saved by Fritzing 0.9.3b)

parts:
  Componente1 = Arduino Nano (Rev3.0)
  Componente3 = Barometric Pressure Sensor - BMP180 Breakout (GY-68)
  KY-1 = Keyes Photo Resistor Sensor [package=THT]
  Mod1 = Nano-V3-0-IO-Expansion-Adapter
  Componente4 = Bluetooth HC-06
  neopixel1 = Neopixel Ring 16
  Part1 = KY-001 Temperature Sensor Module [package="Breakout board"]

nets:
  N1: Componente1.D1/TX, Mod1.D1/TX
  N2: Componente1.D0/RX, Mod1.D0/RX
  N3: Componente1.RESET, Mod1.RST
  GND: Componente1.GND, Componente3.GND, KY-1.ground, Mod1.GND, Componente4.GND, neopixel1.Gnd, Part1.-
  N4: Componente1.D2, Mod1.D2, Componente4.RXD
  N5: Componente1.D3, Mod1.D3_PWM, Componente4.TXD
  N6: Componente1.D4, Mod1.D4, neopixel1.DI
  N7: Componente1.D5, Mod1.D5_PWM, Part1.S
  N8: Componente1.D6, Mod1.D6_PWM
  N9: Componente1.D7, Mod1.D7
  N10: Componente1.D8, Mod1.D8
  N11: Componente1.D9, Mod1.D9_PWM
  N12: Componente1.D10, Mod1.D10_PWM/SS
  N13: Componente1.D11/MOSI, Mod1.D11_PWM/MOSI
  N14: Componente1.D12/MISO, Mod1.D12/MISO
  VIN: Componente1.VIN, Mod1.VIN
  VCC: Componente1.5V, Componente3.VCC, KY-1.power, Mod1.VCC, Componente4.VCC, neopixel1.5V, Part1.Vin
  N15: Componente1.A7, Mod1.A7
  N16: Componente1.A6, Mod1.A6
  N17: Componente1.A5, Componente3.SCL, Mod1.A5/SCL
  N18: Componente1.A4, Componente3.SDA, Mod1.A4/SDA
  N19: Componente1.A3, Mod1.A3
  N20: Componente1.A2, Mod1.A2
  N21: Componente1.A1, Mod1.A1
  N22: Componente1.A0, KY-1.signal, Mod1.A0
  N23: Componente1.AREF, Mod1.AREF
  N24: Componente1.3V3, Mod1.NC
  N25: Componente1.D13/SCK, Mod1.D13/SCK

custom parts:
  Keyes Photo Resistor Sensor: Keyes Photo Resistor Sensor Module for Arduino.
  Nano-V3-0-IO-Expansion-Adapter: Nano V3.0 IO Expansion Adapter Shield. Note pcb view has been supressed as not useful. You can drag a Nano over the Nano connectors and it will connect and appear in schematic (although at present due to a bug, routing will not show as complete in breadboard).
  Neopixel Ring 16: Neopixel Ring x16
  KY-001 Temperature Sensor Module: Arduino Temperature Sensor Module Keyes KY-001, Allows ambient temperature measurement using digital serial bus (DS18B20)
